// Digital circuit main.dig as structural Verilog
module main (
  input  in_1,
  input  in_2,
  input  in_3,
  input  in_4,
  input  in_5,
  input  in_6,
  input  in_7,
  input  in_8,
  input  in_9,
  input  in_10,
  input  in_11,
  input  in_12,
  output [7:0] out_13,
  output [7:0] out_14,
  output [7:0] out_15
);

  Temporary_register TMP (.o(out_13), .i(out_15), .s(in_12));
  registro R0 (.in(out_15), .out(out_15), .s(in_1), .e(in_2));
  registro R1 (.in(out_15), .out(out_15), .s(in_3), .e(in_4));
  registro R2 (.in(out_15), .out(out_15), .s(in_5), .e(in_6));
  registro R3 (.in(out_15), .out(out_15), .s(in_7), .e(in_8));
  MAR MAR (.out(out_14), .in(out_15), .s(in_9));
  RAM RAM (.a(out_14), .s(in_10), .e(in_11), .o(out_15), .i(out_15));
endmodule
