// Digital circuit main_PC_clark.dig as structural Verilog
module main_PC_clark (
);

  mem_1byte mem_1byte_1 ();  // open: i, i_2, i_3, i_4, i_5, i_6, i_7, i_8, s, o, o_2, o_3, o_4, o_5, o_6, o_7, o_8
endmodule
